# Fritzing sketch ControlBoard (saved by Fritzing 0.9.3b)
circuit board: 37.5001cm x 5.49999cm
breadboards: 4

parts:
  LED1 = LED - 5mm [color="Red (633nm)" package="5 mm [THT]"]
  LED2 = LED - 5mm [color="Red (633nm)" package="5 mm [THT]"]
  LED3 = LED - 5mm [color="Red (633nm)" package="5 mm [THT]"]
  LED4 = LED - 5mm [color="Red (633nm)" package="5 mm [THT]"]
  LED5 = LED - 5mm [color="Red (633nm)" package="5 mm [THT]"]
  LED6 = LED - 5mm [color="Red (633nm)" package="5 mm [THT]"]
  LED7 = LED - 5mm [color="Red (633nm)" package="5 mm [THT]"]
  LED8 = LED - 5mm [color="Red (633nm)" package="5 mm [THT]"]
  LED9 = LED - 5mm [color="Green (555nm)" package="5 mm [THT]"]
  R1 = Resistor [tolerance=±5% resistance=1k package=THT]
  R2 = Resistor [tolerance=±5% resistance=1k package=THT]
  R3 = Resistor [tolerance=±5% resistance=1k package=THT]
  R4 = Resistor [tolerance=±5% resistance=1k package=THT]
  R5 = Resistor [tolerance=±5% resistance=1k package=THT]
  R6 = Resistor [tolerance=±5% resistance=1k package=THT]
  R7 = Resistor [tolerance=±5% resistance=1k package=THT]
  R8 = Resistor [tolerance=±5% resistance=1k package=THT]
  R9 = Resistor [tolerance=±5% resistance=1k package=THT]
  R12 = Resistor [tolerance=±5% resistance=39k package=THT]
  R20 = Resistor [tolerance=±5% resistance=39k package=THT]
  R21 = Resistor [tolerance=±5% resistance=39k package=THT]
  R23 = Resistor [tolerance=±5% resistance=39k package=THT]
  R24 = Resistor [tolerance=±5% resistance=39k package=THT]
  SHR_REL = 74HC595 [package="DIP16 [THT]"]
  SHR_LED = 74HC595 [package="DIP16 [THT]"]
  BRAIN = Iskra Mini
  R29 = Resistor [tolerance=±5% resistance=33k package=THT]
  S8 = RightAngleButton [package="[THT]"]
  S7 = RightAngleButton [package="[THT]"]
  S6 = RightAngleButton [package="[THT]"]
  S5 = RightAngleButton [package="[THT]"]
  S4 = RightAngleButton [package="[THT]"]
  S3 = RightAngleButton [package="[THT]"]
  S2 = RightAngleButton [package="[THT]"]
  S1 = RightAngleButton [package="[THT]"]
  S9 = RightAngleButton [package="[THT]"]
  S10 = RightAngleButton [package="[THT]"]
  S11 = RightAngleButton [package="[THT]"]
  RELAY_CTL = male pin header, 9 pins [form="♂ (male)"]
  MIDI_IN = male pin header, 3 pins [form="♂ (male)"]
  LCD_DATA = male pin header, 14 pins [form="♂ (male)"]
  LCD_LED = male pin header, 2 pins [form="♂ (male)"]
  5V = male pin header, 4 pins [form="♂ (male)"]
  MUTE_CTL = male pin header, 1 pin [form="♂ (male)"]
  U1 = 74HC165 [package="DIP16 [THT]"]
  R31 = Resistor [tolerance=±5% resistance=39k package=THT]
  R32 = Resistor [tolerance=±5% resistance=39k package=THT]
  R33 = Resistor [tolerance=±5% resistance=39k package=THT]
  R34 = Resistor [tolerance=±5% resistance=39k package=THT]
  R35 = Resistor [tolerance=±5% resistance=39k package=THT]
  R36 = Resistor [tolerance=±5% resistance=39k package=THT]
  R37 = Resistor [tolerance=±5% resistance=39k package=THT]
  U2 = 74HC165 [package="DIP16 [THT]"]
  RE1 = Rotary Encoder Vertical [package=THT]
  LCD1 = LCD MT-16S2H  # not connected
  R38 = Resistor [tolerance=±5% resistance=39k package=THT]
  X1 = USB Connectors [package=usb-microb]
  J1 = male pin header, 4 pins [form="♂ (male)"]
  Pad1 = Pad [width=5.503333333333333 height=5.9266666666666667 connect=center]  # not connected
  Pad2 = Pad [width=7.9727777777777771 height=5.7149999999999999 connect=center]  # not connected
  MIDI_OUT = male pin header, 1 pin [form="♂ (male)"]

nets:
  N1: LED1.cathode, R1.Pin_1
  N2: LED1.anode, SHR_LED.Q0
  N3: LED2.cathode, R2.Pin_1
  N4: LED2.anode, SHR_LED.Q1
  N5: LED3.cathode, R3.Pin_1
  N6: LED3.anode, SHR_LED.Q2
  N7: LED4.cathode, R4.Pin_1
  N8: LED4.anode, SHR_LED.Q3
  N9: LED5.cathode, R5.Pin_1
  N10: LED5.anode, SHR_LED.Q4
  N11: LED6.cathode, R6.Pin_1
  N12: LED6.anode, SHR_LED.Q5
  N13: LED7.cathode, R7.Pin_1
  N14: LED7.anode, SHR_LED.Q6
  N15: LED8.cathode, R8.Pin_1
  N16: LED8.anode, SHR_LED.Q7
  N17: LED9.cathode, R9.Pin_1
  LED9: LED9.anode, BRAIN.A3
  GND: R1.Pin_0, R2.Pin_0, R3.Pin_0, R4.Pin_0, R5.Pin_0, R6.Pin_0, R7.Pin_0, R8.Pin_0, R9.Pin_0, R12.Pin_1, R20.Pin_1, R21.Pin_1, R23.Pin_1, R24.Pin_1, SHR_REL.GND, SHR_REL.OE, SHR_LED.GND, SHR_LED.OE, BRAIN.GND, R29.Pin_1, RELAY_CTL.pin1, MIDI_IN.pin1, MIDI_IN.pin3, LCD_DATA.pin1, LCD_DATA.pin3, LCD_DATA.pin5, LCD_LED.pin2, 5V.pin2, 5V.pin3, U1.GND, U1.CLK_INH, R31.Pin_1, R32.Pin_1, R33.Pin_1, R34.Pin_1, R35.Pin_1, R36.Pin_1, R37.Pin_1, U2.E, U2.F, U2.G, U2.H, U2.GND, U2.SER, U2.C, U2.CLK_INH, R38.Pin_1
  S9: R12.Pin_0, S9.Pin_1, U2.B
  RE_A: R20.Pin_0, BRAIN.D13, RE1.EncoderPinA
  RE_B: R21.Pin_0, BRAIN.D12, RE1.EncoderPinB
  S11: R23.Pin_0, S11.Pin_1, U2.D
  S10: R24.Pin_0, S10.Pin_1, U2.A
  N18: SHR_REL.Q1, RELAY_CTL.pin3
  N19: SHR_REL.Q2, RELAY_CTL.pin4
  N20: SHR_REL.Q3, RELAY_CTL.pin5
  N21: SHR_REL.Q4, RELAY_CTL.pin6
  N22: SHR_REL.Q5, RELAY_CTL.pin7
  N23: SHR_REL.Q6, RELAY_CTL.pin8
  N24: SHR_REL.Q7, RELAY_CTL.pin9
  N25: SHR_REL.Q7', SHR_LED.DS
  5V: SHR_REL.MR, SHR_REL.VCC, SHR_LED.MR, SHR_LED.VCC, BRAIN.5V, S8.Pin_2, S7.Pin_2, S6.Pin_2, S5.Pin_2, S4.Pin_2, S3.Pin_2, S2.Pin_2, S1.Pin_2, S9.Pin_2, S10.Pin_2, S11.Pin_2, LCD_DATA.pin2, LCD_LED.pin1, 5V.pin1, 5V.pin4, U1.VCC, U2.VCC, RE1.EncoderPinC
  SH_CP/SH_IN_CLK: SHR_REL.SH_CP, SHR_LED.SH_CP, BRAIN.A1, U1.CLK, U2.CLK
  ST_CP: SHR_REL.ST_CP, SHR_LED.ST_CP, BRAIN.D10_PWM
  DS/SH_IN_DATA: SHR_REL.DS, BRAIN.A2, U1.QH'
  N26: SHR_REL.Q0, RELAY_CTL.pin2
  N27: BRAIN.D0/TX, MIDI_OUT.pin1
  N28: BRAIN.D1/RX, MIDI_IN.pin2
  LCD RS: BRAIN.D2, LCD_DATA.pin4
  LCD E: BRAIN.D3_PWM, LCD_DATA.pin6
  LCD DB4: BRAIN.D4, LCD_DATA.pin11
  LCD DB5: BRAIN.D5_PWM, LCD_DATA.pin12
  LCD DB6: BRAIN.D6_PWM, LCD_DATA.pin13
  LCD DB7: BRAIN.D7, LCD_DATA.pin14
  N29: BRAIN.D8, R29.Pin_0, MUTE_CTL.pin1
  SH_IN_LD: BRAIN.A0, U1.SH/LD, U2.SH/LD
  S8: S8.Pin_1, U1.E, R38.Pin_0
  S7: S7.Pin_1, U1.F, R37.Pin_0
  S6: S6.Pin_1, U1.G, R36.Pin_0
  S5: S5.Pin_1, U1.H, R35.Pin_0
  S4: S4.Pin_1, U1.D, R34.Pin_0
  S3: S3.Pin_1, U1.C, R33.Pin_0
  S2: S2.Pin_1, U1.B, R32.Pin_0
  S1: S1.Pin_1, U1.A, R31.Pin_0
  N30: U1.SER, U2.QH
  N31: X1.D+, J1.pin2
  N32: X1.D-, J1.pin3
  N33: X1.GND, J1.pin1
  N34: X1.VBUS, J1.pin4

notes:
  MIDIPatchMate
  14
  1
  +5V
  GND
  E
  RS
  2018.10.19
  +5v

custom parts:
  Iskra Mini: The Arduino Mini is a small microcontroller board originally based on the ATmega168, but now supplied with the 328.(datasheet), intended for use on breadboards and when space is at a premium. It has 14 digital input/output pins (of which 6 can be used as PWM outputs), 8 analog inputs, and a 16 MHz crystal oscillator. It can be programmed with the USB Serial adapter or other USB or RS232 to TTL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
  RightAngleButton: Right Angle Tactile Push Button
  74HC165: 8-bit parallel-load shift registers
  Rotary Encoder Vertical: Rotary Encoder from Bourns PEC16-2215F-N0024.
  LCD MT-16S2H: A standard character display, usually with 2x16 characters. Comes in many colors.
