# Fritzing sketch PatchMateLite (saved by Fritzing 0.9.3b)
circuit board: 19.9859cm x 11.4986cm
breadboards: 1

parts:
  VR = Voltage Regulator [package=to220-igo]
  D2 = Rectifier Diode [part_number=1N4001 package="300 mil [THT]"]
  SEND2 = DS2Y-5-DC5V [part_number=DS2Y-5-DC5V]
  RET2 = DS2Y-5-DC5V [part_number=DS2Y-5-DC5V]
  MUTE_MAIN = DS2Y-5-DC5V [part_number=DS2Y-5-DC5V]
  R1 = Resistor [tolerance=±5% resistance=220 package=THT]
  D1 = Rectifier Diode [part_number=1N4001 package="300 mil [THT]"]
  R4 = Resistor [tolerance=±5% resistance=470 package=THT]
  R3 = Resistor [tolerance=±5% resistance=10k package=THT]
  R2 = Resistor [tolerance=±5% resistance=220 package=THT]
  Power9v = Power plug
  6N139 = 6N138 DIP - 8 pins [package="DIP (Dual Inline) [THT]"]
  R5 = Resistor [tolerance=±5% resistance=470 package=THT]
  R6 = Resistor [tolerance=±5% resistance=470 package=THT]
  Q1 = NPN-Transistor [package="TO92 [THT]"]
  R7 = Resistor [tolerance=±5% resistance=4.7k package=THT]
  D3 = Rectifier Diode [part_number=1N4001 package="300 mil [THT]"]
  SEND1 = DS2Y-5-DC5V [part_number=DS2Y-5-DC5V]
  RET1 = DS2Y-5-DC5V [part_number=DS2Y-5-DC5V]
  S4/right = RightAngleButton [package="[THT]"]
  S5/left = RightAngleButton [package="[THT]"]
  R10 = Resistor [tolerance=±5% resistance=39k package=THT]
  R11 = Resistor [tolerance=±5% resistance=39k package=THT]
  R12 = Resistor [tolerance=±5% resistance=39k package=THT]
  R9 = Resistor [tolerance=±5% resistance=39k package=THT]
  S2 = RightAngleButton [package="[THT]"]
  S1 = RightAngleButton [package="[THT]"]
  LED2 = LED - 5mm [color="Red (633nm)" package="5 mm [THT]"]
  LED1 = LED - 5mm [color="Red (633nm)" package="5 mm [THT]"]
  R17 = Resistor [tolerance=±5% resistance=1k package=THT]
  R15 = Resistor [tolerance=±5% resistance=1k package=THT]
  R18 = Resistor [tolerance=±5% resistance=39k package=THT]
  S3/store = RightAngleButton [package="[THT]"]
  LED3 = LED - 5mm [color="Green (555nm)" package="5 mm [THT]"]
  R13 = Resistor [tolerance=±5% resistance=1k package=THT]
  R14 = Resistor [tolerance=±5% resistance=39k package=THT]
  U1 = 74HC595 [package="DIP16 [THT]"]
  IC1 = ULN2003A [package="DIP16 [THT]"]
  R16 = Resistor [tolerance=±5% resistance=39k package=THT]
  Iskra1 = Iskra Mini
  J1 = female pin header, 14 pins [form="♀ (female)"]
  J2 = female pin header, 2 pins [form="♀ (female)"]
  LOOP2 = Double Jack 6.3 [package=ACJS-MHDR]
  LOOP1 = Double Jack 6.3 [package=ACJS-MHDR]
  R8 = Resistor [tolerance=±5% resistance=10k package=THT]
  Pad1 = Pad [width=19.760000000000002 height=6.21 connect=center]  # not connected
  Pad2 = Pad [width=19.755555555555556 height=6.2088794814814809 connect=center]  # not connected
  Pad3 = Pad [width=9.0311111111111106 height=12.558888888888889 connect=center]  # not connected
  U2 = 74HC165 [package="DIP16 [THT]"]
  MIDI_IN = DIN-5 jack (MIDI) [part_number=DS-5-01 package=THTw]
  MIDI_THRU = DIN-5 jack (MIDI) [part_number=DS-5-01 package=THTw]
  C1 = Tantalum Capacitor [capacitance=0.1µF voltage=16V package="200 mil [THT, tantalum]"]
  C2 = Tantalum Capacitor [capacitance=22µF package="200 mil [THT, tantalum]"]
  VDS1 = Bridge Rectifier [part_number=KBL4005 package=kbl]
  Pad4 = Pad [width=59 height=2 connect=center]
  Pad5 = Pad [width=52.493333333333332 height=2 connect=center]
  Pad6 = Pad [width=20.461111111111112 height=2 connect=center]
  MAIN_INPUT = Neutrik - NMJ6HFD2-AU [package=NMJ6HFD2-AU]
  MAIN_OUT = Neutrik - NMJ6HFD2-AU [package=NMJ6HFD2-AU]
  RE1 = Rotary Encoder Vertical [package=THT]

nets:
  N1: VR.IN, C1.+, VDS1.+
  5V: VR.OUT, SEND2.1_+, RET2.1_+, MUTE_MAIN.1_+, R4.Pin_0, R2.Pin_1, 6N139.pin8, D3.cathode, SEND1.1_+, RET1.1_+, S4/right.Pin_2, S5/left.Pin_2, S2.Pin_2, S1.Pin_2, S3/store.Pin_2, U1.MR, U1.VCC, IC1.COM_-_Common, Iskra1.5V, J1.pin2, J2.pin1, U2.VCC, C2.+, RE1.EncoderPinC
  GND: VR.GND, R3.Pin_0, 6N139.pin5, Q1.E, R10.Pin_1, R11.Pin_1, R12.Pin_1, R9.Pin_1, R17.Pin_0, R15.Pin_0, R18.Pin_0, R13.Pin_0, R14.Pin_1, U1.GND, U1.OE, IC1.0V, R16.Pin_0, Iskra1.GND, J1.pin1, J1.pin3, J1.pin5, J2.pin2, R8.Pin_0, U2.E, U2.F, U2.GND, U2.SER, U2.CLK_INH, MIDI_THRU.2, C1.-, C2.-, VDS1.-, Pad4.pad, Pad5.pad, Pad6.pad
  RX-MIDI_IN: D2.cathode, R4.Pin_1, 6N139.pin6, Iskra1.D1/RX
  N2: D2.anode, MIDI_THRU.5
  N3: SEND2.8_N.O., LOOP2.2_Ring_(8)
  N4: SEND2.6_N.C., RET2.6_N.C.
  N5: SEND2.4_COM, RET1.4_COM
  LOOP2: SEND2.16_-, RET2.16_-, IC1.Out_6
  N6: SEND2.13_COM, RET1.13_COM
  N7: SEND2.11_N.C., RET2.11_N.C.
  N8: SEND2.9_N.O., LOOP2.2_Tip_(9)
  N9: RET2.8_N.O., LOOP2.Ring_(2)
  N10: RET2.4_COM, MUTE_MAIN.11_N.C., MAIN_OUT.Ring_(5)
  N11: RET2.13_COM, MUTE_MAIN.6_N.C., MAIN_OUT.Tip_(6)
  N12: RET2.9_N.O., LOOP2.Tip_(3)
  N13: MUTE_MAIN.4_COM, R6.Pin_0
  N14: MUTE_MAIN.16_-, Q1.C, D3.anode
  N15: MUTE_MAIN.13_COM, R5.Pin_0
  N16: R1.Pin_0, MIDI_IN.4
  N17: R1.Pin_1, D1.cathode, 6N139.pin2
  N18: D1.anode, 6N139.pin3, MIDI_IN.5
  N19: R3.Pin_1, 6N139.pin7
  N20: R2.Pin_0, MIDI_THRU.4
  N21: Power9v.GND, VDS1.~#2
  N22: Power9v.VCC, VDS1.~#1
  sleeve: R5.Pin_1, R6.Pin_1, LOOP2.Sleeve_(1), LOOP2.Sleeve_S_(4), LOOP2.2_Sleeve_(7), LOOP2.2_Sleeve_S_(10), LOOP1.Sleeve_(1), LOOP1.Sleeve_S_(4), LOOP1.2_Sleeve_(7), LOOP1.2_Sleeve_S_(10), MAIN_INPUT.Sleeve_(1), MAIN_INPUT.Sleeve_(4), MAIN_OUT.Sleeve_(1), MAIN_OUT.Sleeve_(4)
  N23: Q1.B, R7.Pin_1
  MUTE: R7.Pin_0, Iskra1.D4, R8.Pin_1
  N24: SEND1.8_N.O., LOOP1.2_Ring_(8)
  N25: SEND1.6_N.C., RET1.6_N.C.
  N26: SEND1.4_COM, MAIN_INPUT.Ring_(5)
  LOOP1: SEND1.16_-, RET1.16_-, IC1.Out_7
  N27: SEND1.13_COM, MAIN_INPUT.Tip_(6)
  N28: SEND1.11_N.C., RET1.11_N.C.
  N29: SEND1.9_N.O., LOOP1.2_Tip_(9)
  N30: RET1.8_N.O., LOOP1.Ring_(2)
  N31: RET1.9_N.O., LOOP1.Tip_(3)
  N32: S4/right.Pin_1, R12.Pin_0, U2.A
  N33: S5/left.Pin_1, R9.Pin_0, U2.G
  ENC_B: R10.Pin_0, Iskra1.D10_PWM, RE1.EncoderPinA
  ENC_A: R11.Pin_0, Iskra1.D12, RE1.EncoderPinB
  N34: S2.Pin_1, R16.Pin_1, U2.D
  N35: S1.Pin_1, R18.Pin_1, U2.C
  N36: LED2.cathode, R15.Pin_1
  LED2: LED2.anode, U1.Q1
  N37: LED1.cathode, R17.Pin_1
  LED1: LED1.anode, U1.Q2
  STORE: S3/store.Pin_1, R14.Pin_0, Iskra1.A0
  N38: LED3.cathode, R13.Pin_1
  STORE_LED: LED3.anode, Iskra1.D13
  N39: U1.Q3, IC1.In_7
  N40: U1.Q4, IC1.In_6
  PS_CLK/SH_CP: U1.SH_CP, Iskra1.A2, U2.CLK
  ST_CP: U1.ST_CP, Iskra1.D11_PWM
  DS/PS_QH: U1.DS, Iskra1.A3, U2.QH'
  N41: Iskra1.D2, J1.pin4
  N42: Iskra1.D3_PWM, J1.pin6
  N43: Iskra1.D5_PWM, J1.pin14
  N44: Iskra1.D6_PWM, J1.pin13
  N45: Iskra1.D7, J1.pin12
  N46: Iskra1.D8, J1.pin11
  PS_LD: Iskra1.A1, U2.SH/LD

notes:
  MIDIPatchMate (Lite), 07.20
  MIDIPatchMate (Lite)
  02.08.2018

custom parts:
  Voltage Regulator: Voltage Regulator Standard L4940V5 5V regulator. IGO (Input Ground Output). ST Microelectronics
  DS2Y-5-DC5V: Panasonic DS2Y-5-DC5V Relay with 2 form C contact
  6N138 DIP - 8 pins: A DIP stand-in part for whatever IC you want. With 8 pins on a 300mil dual inline package (DIP) footprint.
  RightAngleButton: Right Angle Tactile Push Button
  Iskra Mini: The Arduino Mini is a small microcontroller board originally based on the ATmega168, but now supplied with the 328.(datasheet), intended for use on breadboards and when space is at a premium. It has 14 digital input/output pins (of which 6 can be used as PWM outputs), 8 analog inputs, and a 16 MHz crystal oscillator. It can be programmed with the USB Serial adapter or other USB or RS232 to TTL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
  Double Jack 6.3: DOUBLE - JACK, 6.35MM, PCB, STEREO)
  74HC165: 8-bit parallel-load shift registers
  DIN-5 jack (MIDI): Female DIN connector with 5 pins, as used for MIDI and SYNC
  Bridge Rectifier: Single-Phase Bridge Rectifier KBL005 thru KBL10 Vishay Semiconductors formerly General Semiconductor ReverseVoltage 50 and 1000V Forward Current 4.0 A
  Neutrik - NMJ6HFD2-AU: Neutrik - NMJ6HFD2-AU - JACK, 6.35MM, PCB, STEREO)
  Rotary Encoder Vertical: Rotary Encoder from Bourns PEC16-2215F-N0024.
