# Fritzing sketch RelayBoard (saved by Fritzing 0.9.3b)
circuit board: 38.5cm x 8.7cm
breadboards: 1

parts:
  R25 = Resistor [tolerance=±5% resistance=220 package=THT]
  D1 = Rectifier Diode [part_number=1N4001 package="300 mil [THT]"]
  R26 = Resistor [tolerance=±5% resistance=470 package=THT]
  R27 = Resistor [tolerance=±5% resistance=10k package=THT]
  R28 = Resistor [tolerance=±5% resistance=220 package=THT]
  6N138 = 6N138 DIP - 8 pins [package="DIP (Dual Inline) [THT]"]
  U1 = ULN2803A [package=THT]
  RELAY_CTL = male pin header, 9 pins [form="♂ (male)"]
  LOOP1 = Double Jack 6.3 [package=ACJS-MHDR]
  LOOP2 = Double Jack 6.3 [package=ACJS-MHDR]
  LOOP3 = Double Jack 6.3 [package=ACJS-MHDR]
  LOOP4 = Double Jack 6.3 [package=ACJS-MHDR]
  OUT4/IN5 = Double Jack 6.3 [package=ACJS-MHDR]
  LOOP5 = Double Jack 6.3 [package=ACJS-MHDR]
  LOOP6 = Double Jack 6.3 [package=ACJS-MHDR]
  LOOP7 = Double Jack 6.3 [package=ACJS-MHDR]
  LOOP8 = Double Jack 6.3 [package=ACJS-MHDR]
  D2 = Rectifier Diode [part_number=1N4001 package="300 mil [THT]"]
  MIDI_IN = male pin header, 3 pins [form="♂ (male)"]
  VR1 = Voltage Regulator [package=to220-igo]
  R29 = Resistor [tolerance=±5% resistance=470 package=THT]
  R30 = Resistor [tolerance=±5% resistance=470 package=THT]
  Q1 = NPN-Transistor [package="TO92 [THT]"]
  R31 = Resistor [tolerance=±5% resistance=4.7k package=THT]
  D3 = Rectifier Diode [part_number=1N4001 package="300 mil [THT]"]
  R32 = Resistor [tolerance=±5% resistance=470 package=THT]
  R33 = Resistor [tolerance=±5% resistance=470 package=THT]
  5V = male pin header, 4 pins [form="♂ (male)"]
  MUTE_CTL = male pin header, 1 pin [form="♂ (male)"]
  Pad1 = Pad [width=23.236296296296292 height=19.849629629629622 connect=center]  # not connected
  Pad2 = Pad [width=19.191205185185186 height=6.9614720740740683 connect=center]  # not connected
  Pad3 = Pad [width=19.285194592592596 height=6.8673979999999997 connect=center]  # not connected
  C1 = Tantalum Capacitor [capacitance=100nF voltage=16V package="200 mil [THT, tantalum]"]
  C2 = Tantalum Capacitor [capacitance=22µF package="200 mil [THT, tantalum]"]
  MIDI_THRU = DIN-5 jack (MIDI) [part_number=DS-5-01 package=THTw]
  MIDI_IN_2 = DIN-5 jack (MIDI) [part_number=DS-5-01 package=THTw]
  VDS1 = Bridge Rectifier [part_number=KBL4005 package=kbl]
  MAIN_INPUT = Neutrik - NMJ6HFD2-AU [package=NMJ6HFD2-AU]
  MAIN_OUT = Neutrik - NMJ6HFD2-AU [package=NMJ6HFD2-AU]
  VR2 = Voltage Regulator [package="ddpack to-263"]
  C4 = Electrolytic Capacitor [capacitance=100µF voltage=16V package="100 mil [THT, electrolytic]"]
  L1 = Inductor [inductance=100µH package="400 mil [THT]"]
  VR_SELECT = male pin header, 3 pins [form="♂ (male)"]
  5V_SELECT = male pin header, 3 pins [form="♂ (male)"]
  POWER_LED = male pin header, 2 pins [form="♂ (male)"]
  POWER_SWITCH = male pin header, 2 pins [form="♂ (male)"]
  VR2_2 = Pad [width=17.836444444444446 height=23.706666666666667 connect=center]  # not connected
  C3 = Electrolytic Capacitor [capacitance=1mF package="3.5 mm [THT, electrolytic]"]
  VR2a = LM2575 TO220 Straight leads [package=TO-220-KC]
  D5 = Schottky Diode [part_number=1N5822 package="600 mil [THT]"]
  MUTE_MAIN = D2n [part_number=8-1393792-5]
  SEND8 = D2n [part_number=8-1393792-5]
  RET8 = D2n [part_number=8-1393792-5]
  SEND7 = D2n [part_number=8-1393792-5]
  RET7 = D2n [part_number=8-1393792-5]
  SEND6 = D2n [part_number=8-1393792-5]
  RET6 = D2n [part_number=8-1393792-5]
  SEND5 = D2n [part_number=8-1393792-5]
  RET5 = D2n [part_number=8-1393792-5]
  MUTE4 = D2n [part_number=8-1393792-5]
  SEND4 = D2n [part_number=8-1393792-5]
  RET4 = D2n [part_number=8-1393792-5]
  RET3 = D2n [part_number=8-1393792-5]
  SEND3 = D2n [part_number=8-1393792-5]
  SEND2 = D2n [part_number=8-1393792-5]
  RET2 = D2n [part_number=8-1393792-5]
  SEND1 = D2n [part_number=8-1393792-5]
  RET1 = D2n [part_number=8-1393792-5]
  MIDI_OUT = DIN-5 jack (MIDI) [part_number=DS-5-01 package=THTw]
  R34 = Resistor [tolerance=±5% resistance=220 package=THT]
  R35 = Resistor [tolerance=±5% resistance=220 package=THT]
  MIDI_OUT_2 = male pin header, 1 pin [form="♂ (male)"]
  Pad4 = Pad [width=19.47333333333334 height=6.7733333333333325 connect=center]  # not connected
  Power_9v = Power plug [part_number=DS-210]
  D6 = Rectifier Diode [part_number=1N4001 package="300 mil [THT]"]

nets:
  N1: R25.Pin_0, MIDI_IN_2.4
  N2: R25.Pin_1, D1.cathode, 6N138.pin2
  N3: D1.anode, 6N138.pin3, MIDI_IN_2.5
  5V: R26.Pin_0, R28.Pin_1, 6N138.pin8, U1.COM_-_Common, D3.cathode, 5V.pin1, 5V.pin4, 5V_SELECT.pin2, POWER_LED.pin1, MUTE_MAIN.1_+, SEND8.1_+, RET8.1_+, SEND7.1_+, RET7.1_+, SEND6.1_+, RET6.1_+, SEND5.1_+, RET5.1_+, MUTE4.1_+, SEND4.1_+, RET4.1_+, RET3.1_+, SEND3.1_+, SEND2.1_+, RET2.1_+, SEND1.1_+, RET1.1_+, R34.Pin_1, D6.cathode
  N4: R26.Pin_1, 6N138.pin6, D2.cathode, MIDI_IN.pin2
  GND: R27.Pin_0, 6N138.pin5, MIDI_IN.pin1, MIDI_IN.pin3, VR1.GND, Q1.E, 5V.pin2, 5V.pin3, C1.-, C2.-, MIDI_THRU.2, VDS1.-, VR2.GND, VR2.ON/OFF, C4.-, POWER_LED.pin2, C3.-, VR2a.GND, VR2a.ON/OFF, D5.anode, MIDI_OUT.2
  N5: R27.Pin_1, 6N138.pin7
  N6: R28.Pin_0, MIDI_THRU.4
  N7: U1.In_1, RELAY_CTL.pin9
  N8: U1.In_2, RELAY_CTL.pin8
  N9: U1.In_3, RELAY_CTL.pin7
  N10: U1.In_4, RELAY_CTL.pin6
  N11: U1.In_5, RELAY_CTL.pin5
  N12: U1.In_6, RELAY_CTL.pin4
  N13: U1.In_7, RELAY_CTL.pin3
  N14: U1.In_8, RELAY_CTL.pin2
  N15: U1.0V, RELAY_CTL.pin1
  N16: U1.Out_8, SEND1.16_-, RET1.16_-
  N17: U1.Out_7, SEND2.16_-, RET2.16_-
  N18: U1.Out_6, RET3.16_-, SEND3.16_-
  N19: U1.Out_5, SEND4.16_-, RET4.16_-
  N20: U1.Out_4, SEND5.16_-, RET5.16_-
  N21: U1.Out_3, SEND6.16_-, RET6.16_-
  N22: U1.Out_2, SEND7.16_-, RET7.16_-
  N23: U1.Out_1, SEND8.16_-, RET8.16_-
  sleeve: LOOP1.Sleeve_(1), LOOP1.Sleeve_S_(4), LOOP1.2_Sleeve_(7), LOOP1.2_Sleeve_S_(10), LOOP2.Sleeve_(1), LOOP2.Sleeve_S_(4), LOOP2.2_Sleeve_(7), LOOP2.2_Sleeve_S_(10), LOOP3.Sleeve_(1), LOOP3.Sleeve_S_(4), LOOP3.2_Sleeve_(7), LOOP3.2_Sleeve_S_(10), LOOP4.Sleeve_(1), LOOP4.Sleeve_S_(4), LOOP4.2_Sleeve_(7), LOOP4.2_Sleeve_S_(10), OUT4/IN5.Sleeve_(1), OUT4/IN5.Sleeve_S_(4), OUT4/IN5.2_Sleeve_(7), OUT4/IN5.2_Sleeve_S_(10), LOOP5.Sleeve_(1), LOOP5.Sleeve_S_(4), LOOP5.2_Sleeve_(7), LOOP5.2_Sleeve_S_(10), LOOP6.Sleeve_(1), LOOP6.Sleeve_S_(4), LOOP6.2_Sleeve_(7), LOOP6.2_Sleeve_S_(10), LOOP7.Sleeve_(1), LOOP7.Sleeve_S_(4), LOOP7.2_Sleeve_(7), LOOP7.2_Sleeve_S_(10), LOOP8.Sleeve_(1), LOOP8.Sleeve_S_(4), LOOP8.2_Sleeve_(7), LOOP8.2_Sleeve_S_(10), R29.Pin_1, R30.Pin_1, R32.Pin_1, R33.Pin_1, MAIN_INPUT.Sleeve_(1), MAIN_INPUT.Sleeve_(4), MAIN_OUT.Sleeve_(1), MAIN_OUT.Sleeve_(4)
  N24: LOOP1.Ring_(2), RET1.8_N.O.
  N25: LOOP1.Tip_(3), RET1.9_N.O.
  N26: LOOP1.2_Ring_(8), SEND1.8_N.O.
  N27: LOOP1.2_Tip_(9), SEND1.9_N.O.
  N28: LOOP2.Ring_(2), RET2.8_N.O.
  N29: LOOP2.Tip_(3), RET2.9_N.O.
  N30: LOOP2.2_Ring_(8), SEND2.8_N.O.
  N31: LOOP2.2_Tip_(9), SEND2.9_N.O.
  N32: LOOP3.Ring_(2), RET3.8_N.O.
  N33: LOOP3.Tip_(3), RET3.9_N.O.
  N34: LOOP3.2_Ring_(8), SEND3.8_N.O.
  N35: LOOP3.2_Tip_(9), SEND3.9_N.O.
  N36: LOOP4.Ring_(2), RET4.8_N.O.
  N37: LOOP4.Tip_(3), RET4.9_N.O.
  N38: LOOP4.2_Ring_(8), SEND4.8_N.O.
  N39: LOOP4.2_Tip_(9), SEND4.9_N.O.
  N40: OUT4/IN5.Ring_(2), OUT4/IN5.2_Ring_S_(11), MUTE4.6_N.C., RET4.4_COM
  N41: OUT4/IN5.Tip_(3), OUT4/IN5.2_Tip_S_(12), MUTE4.11_N.C., RET4.13_COM
  N42: OUT4/IN5.2_Ring_(8), SEND5.4_COM
  N43: OUT4/IN5.2_Tip_(9), SEND5.13_COM
  N44: LOOP5.Ring_(2), RET5.8_N.O.
  N45: LOOP5.Tip_(3), RET5.9_N.O.
  N46: LOOP5.2_Ring_(8), SEND5.8_N.O.
  N47: LOOP5.2_Tip_(9), SEND5.9_N.O.
  N48: LOOP6.Ring_(2), RET6.8_N.O.
  N49: LOOP6.Tip_(3), RET6.9_N.O.
  N50: LOOP6.2_Ring_(8), SEND6.8_N.O.
  N51: LOOP6.2_Tip_(9), SEND6.9_N.O.
  N52: LOOP7.Ring_(2), RET7.8_N.O.
  N53: LOOP7.Tip_(3), RET7.9_N.O.
  N54: LOOP7.2_Ring_(8), SEND7.8_N.O.
  N55: LOOP7.2_Tip_(9), SEND7.9_N.O.
  N56: LOOP8.Ring_(2), RET8.8_N.O.
  N57: LOOP8.Tip_(3), RET8.9_N.O.
  N58: LOOP8.2_Ring_(8), SEND8.8_N.O.
  N59: LOOP8.2_Tip_(9), SEND8.9_N.O.
  N60: D2.anode, MIDI_THRU.5
  +9V #1: VR1.IN, C1.+, VR_SELECT.pin1
  +5V #1: VR1.OUT, C2.+, 5V_SELECT.pin1
  N61: R29.Pin_0, MUTE_MAIN.13_COM
  N62: R30.Pin_0, MUTE_MAIN.4_COM
  N63: Q1.B, R31.Pin_1
  N64: Q1.C, D3.anode, MUTE_MAIN.16_-, MUTE4.16_-, D6.anode
  N65: R31.Pin_0, MUTE_CTL.pin1
  N66: R32.Pin_0, MUTE4.13_COM
  N67: R33.Pin_0, MUTE4.4_COM
  9V: VDS1.+, POWER_SWITCH.pin1
  N68: VDS1.~#1, Power_9v.VCC
  N69: VDS1.~#2, Power_9v.GND
  N70: MAIN_INPUT.Ring_(5), SEND1.4_COM
  N71: MAIN_INPUT.Tip_(6), SEND1.13_COM
  N72: MAIN_OUT.Ring_(5), MUTE_MAIN.11_N.C., RET8.4_COM
  N73: MAIN_OUT.Tip_(6), MUTE_MAIN.6_N.C., RET8.13_COM
  +9V #2: VR2.Vin, C4.+, VR_SELECT.pin3, VR2a.+Vin
  N74: VR2.OUT, L1.pin_0, VR2a.+Vout, D5.cathode
  +5V #2: VR2.Feedback, L1.pin_1, 5V_SELECT.pin3, C3.+, VR2a.Feedback
  N75: VR_SELECT.pin2, POWER_SWITCH.pin2
  N76: SEND8.6_N.C., RET8.6_N.C.
  N77: SEND8.4_COM, RET7.4_COM
  N78: SEND8.13_COM, RET7.13_COM
  N79: SEND8.11_N.C., RET8.11_N.C.
  N80: SEND7.6_N.C., RET7.6_N.C.
  N81: SEND7.4_COM, RET6.4_COM
  N82: SEND7.13_COM, RET6.13_COM
  N83: SEND7.11_N.C., RET7.11_N.C.
  N84: SEND6.6_N.C., RET6.6_N.C.
  N85: SEND6.4_COM, RET5.4_COM
  N86: SEND6.13_COM, RET5.13_COM
  N87: SEND6.11_N.C., RET6.11_N.C.
  N88: SEND5.6_N.C., RET5.6_N.C.
  N89: SEND5.11_N.C., RET5.11_N.C.
  N90: SEND4.6_N.C., RET4.6_N.C.
  N91: SEND4.4_COM, RET3.4_COM
  N92: SEND4.13_COM, RET3.13_COM
  N93: SEND4.11_N.C., RET4.11_N.C.
  N94: RET3.6_N.C., SEND3.6_N.C.
  N95: RET3.11_N.C., SEND3.11_N.C.
  N96: SEND3.4_COM, RET2.4_COM
  N97: SEND3.13_COM, RET2.13_COM
  N98: SEND2.6_N.C., RET2.6_N.C.
  N99: SEND2.4_COM, RET1.4_COM
  N100: SEND2.13_COM, RET1.13_COM
  N101: SEND2.11_N.C., RET2.11_N.C.
  N102: SEND1.6_N.C., RET1.6_N.C.
  N103: SEND1.11_N.C., RET1.11_N.C.
  N104: MIDI_OUT.5, R35.Pin_0
  N105: MIDI_OUT.4, R34.Pin_0
  N106: R35.Pin_1, MIDI_OUT_2.pin1

notes:
  R
  T
  1RS
  RS
  +5v
  GND
  1
  8
  TX
  MIDIPatchMate
  +
  -
  2018.10.10
  2

custom parts:
  6N138 DIP - 8 pins: A DIP stand-in part for whatever IC you want. With 8 pins on a 300mil dual inline package (DIP) footprint.
  Double Jack 6.3: DOUBLE - JACK, 6.35MM, PCB, STEREO)
  Voltage Regulator: Voltage Regulator Standard L4940V5 5V regulator. IGO (Input Ground Output). ST Microelectronics
  DIN-5 jack (MIDI): Female DIN connector with 5 pins, as used for MIDI and SYNC
  Bridge Rectifier: Single-Phase Bridge Rectifier KBL005 thru KBL10 Vishay Semiconductors formerly General Semiconductor ReverseVoltage 50 and 1000V Forward Current 4.0 A
  Neutrik - NMJ6HFD2-AU: Neutrik - NMJ6HFD2-AU - JACK, 6.35MM, PCB, STEREO)
  Voltage Regulator: LM2576/LM2576HV Series SIMPLE SWITCHER® 3A Step-Down Voltage Regulator
  Electrolytic Capacitor: electrolytic capacitor
  LM2575 TO220 Straight leads: LM2575 DC Voltage Regulator TO-220-KC straight leads
  Schottky Diode: A standard schottky barrier rectifier diode
  D2n: AXICOM 2 pole telecom relay, non-polarized, Through Hole Type (THT)
  Power plug: power plug
