# Fritzing sketch USBBoard (saved by Fritzing 0.9.3b)
circuit board: 3.5cm x 4cm
breadboards: 1

parts:
  X2 = USB Connectors [package=usb-b-pth]
  J1 = female pin header, 4 pins [form="♀ (female)"]

nets:
  N1: X2.D+, J1.pin1
  N2: X2.D-, J1.pin2
  N3: X2.GND, J1.pin4
  N4: X2.VBUS, J1.pin3

notes:
  D+
  D-
  GND
  VBUS
